// Logisim project 4BITCOMPUTER.circ as structural Verilog: 1 circuit, main circuit main
module main (
  input  in_1,
  input  in_2,
  input  in_3,
  input  in_4,
  input  in_5,
  input  in_6,
  input  in_7,
  input  in_8,
  input  in_9,
  input  in_10,
  input  in_11,
  input  in_12,
  input  in_13,
  input  in_14,
  input  in_15,
  input  in_16,
  input  in_17,
  input  in_18,
  input  in_19,
  input  in_20,
  input  in_21,
  input  in_22,
  input  in_23,
  input  in_24,
  input  in_25,
  input  in_26,
  input  in_27,
  input  in_28,
  input  in_29,
  input  in_30,
  input  in_31,
  input  in_32,
  input  in_33,
  input  in_34,
  input  in_35,
  input  in_36,
  input  in_37,
  input  in_38,
  input  in_39,
  input  in_40,
  input  in_41,
  input  in_42,
  input  in_43,
  input  in_44,
  input  in_45,
  input  in_46,
  input  in_47,
  input  in_48,
  input  in_49,
  input  in_50,
  input  in_51,
  input  in_52,
  input  in_53,
  output out_54,
  output CAR,
  output out_56,
  output SUM,
  output out_58,
  output CAR_2,
  output out_60,
  output SUM_2,
  output out_62,
  output CAR_3,
  output out_64,
  output SUM_3,
  output out_66,
  output CAR_4,
  output out_68,
  output out_69,
  output out_70,
  output out_71,
  output out_72,
  output out_73,
  output SUM_4,
  output out_75,
  output out_76,
  output out_77,
  output out_78,
  output out_79,
  output out_80,
  output out_81,
  output out_82,
  output out_83,
  output out_84,
  output out_85,
  output out_86
);

  wire and_1_out, and_2_out, and_3_out, and_4_out, and_5_out, and_6_out, and_7_out, and_8_out, and_9_out,
       and_10_out, and_11_out, and_12_out, and_13_out, and_14_out, and_15_out, and_16_out, and_17_out,
       and_18_out, and_19_out, and_20_out, and_21_out, and_22_out, and_23_out, and_24_out, and_25_out,
       and_26_out, and_27_out, and_28_out, and_29_out, and_30_out, and_31_out, and_32_out, and_33_out,
       and_34_out, and_35_out, and_36_out, and_37_out, and_38_out, and_39_out, and_40_out, and_41_out,
       and_42_out, and_43_out, and_44_out, and_45_out, and_46_out, and_47_out, and_48_out, and_49_out,
       and_50_out, and_51_out, and_52_out, and_53_out, and_54_out, and_55_out, and_56_out, and_57_out,
       and_58_out, and_59_out, and_60_out, and_61_out, and_62_out, and_63_out, and_64_out, and_65_out,
       and_66_out, and_67_out, and_68_out, and_69_out, and_70_out, nand_1_out, nand_2_out, nand_3_out,
       nand_4_out, nand_5_out, nand_6_out, nand_7_out, nand_8_out, nand_9_out, nand_10_out, nand_11_out,
       nand_12_out, nand_13_out, nand_14_out, nand_15_out, nand_16_out, nand_17_out, nand_18_out,
       nand_19_out, nand_20_out, nand_21_out, nand_22_out, nand_23_out, nand_24_out, nor_2_out, nor_4_out,
       nor_6_out, nor_8_out, nor_9_out, nor_10_out, nor_11_out, nor_12_out, nor_13_out, nor_14_out,
       nor_15_out, nor_16_out, nor_17_out, nor_18_out, nor_22_out, nor_24_out, nor_25_out, nor_26_out,
       nor_28_out, nor_30_out, nor_32_out, nor_34_out, not_1_out, not_2_out, not_3_out, not_4_out, not_5_out,
       not_6_out, not_7_out, not_8_out, not_9_out, not_10_out, not_11_out, not_12_out, not_13_out,
       not_14_out, not_15_out, not_16_out, not_17_out, not_18_out, not_19_out, not_20_out, not_21_out,
       not_22_out, not_23_out, not_24_out, not_25_out, not_26_out, not_27_out, not_28_out, not_29_out,
       not_30_out, not_31_out, not_32_out, xor_1_out, xor_2_out, xor_3_out, xor_4_out, xor_5_out, xor_7_out,
       xor_9_out, xor_11_out;

  nand nand_1 (nand_1_out, out_58, out_56);
  nand nand_2 (nand_2_out, out_58, out_54);
  nand nand_3 (nand_3_out, out_62, out_60);
  nand nand_4 (nand_4_out, out_62, out_58);
  nand nand_5 (nand_5_out, out_66, out_64);
  nand nand_6 (nand_6_out, out_66, out_62);
  nand nand_7 (nand_7_out, in_5, out_68);
  nand nand_8 (nand_8_out, in_5, out_66);
  nand nand_9 (nand_9_out, nand_1_out, nand_10_out);
  nand nand_10 (nand_10_out, nand_9_out, nand_2_out);
  nand nand_11 (nand_11_out, nand_5_out, nand_12_out);
  nand nand_12 (nand_12_out, nand_11_out, nand_6_out);
  not not_1 (not_1_out, out_58);
  nand nand_13 (nand_13_out, nand_3_out, nand_14_out);
  nand nand_14 (nand_14_out, nand_13_out, nand_4_out);
  not not_2 (not_2_out, out_62);
  not not_3 (not_3_out, out_66);
  nand nand_15 (nand_15_out, nand_7_out, nand_16_out);
  nand nand_16 (nand_16_out, nand_15_out, nand_8_out);
  not not_4 (not_4_out, in_5);
  nand nand_17 (nand_17_out, nand_10_out, not_1_out, not_1_out);
  nand nand_18 (nand_18_out, nand_9_out, not_1_out);
  nand nand_19 (nand_19_out, nand_14_out, not_2_out, not_2_out);
  nand nand_20 (nand_20_out, nand_13_out, not_2_out);
  nand nand_21 (nand_21_out, nand_12_out, not_3_out, not_3_out);
  nand nand_22 (nand_22_out, nand_11_out, not_3_out);
  nand nand_23 (nand_23_out, nand_16_out, not_4_out, not_4_out);
  nand nand_24 (nand_24_out, nand_15_out, not_4_out);
  nand nand_25 (out_56, out_54, nand_17_out);
  nand nand_26 (out_54, nand_18_out, out_56);
  nand nand_27 (out_60, out_58, nand_19_out);
  nand nand_28 (out_58, nand_20_out, out_60);
  nand nand_29 (out_64, out_62, nand_21_out);
  nand nand_30 (out_62, nand_22_out, out_64);
  nand nand_31 (out_68, out_66, nand_23_out);
  nand nand_32 (out_66, nand_24_out, out_68);
  not not_5 (not_5_out, out_54);
  not not_6 (not_6_out, out_58);
  not not_7 (not_7_out, out_62);
  not not_8 (not_8_out, out_66);
  Controlled_Buffer controlled_buffer_1 ();  // open: in, out, en
  assign in_25 = and_11_out ? in_6 : 1'bz;  // Controlled_Buffer controlled_buffer_2
  assign in_27 = and_11_out ? in_7 : 1'bz;  // Controlled_Buffer controlled_buffer_3
  assign in_28 = and_11_out ? in_8 : 1'bz;  // Controlled_Buffer controlled_buffer_4
  assign in_29 = and_11_out ? in_9 : 1'bz;  // Controlled_Buffer controlled_buffer_5
  assign in_1 = and_11_out ? in_10 : 1'bz;  // Controlled_Buffer controlled_buffer_6
  assign in_2 = and_11_out ? in_11 : 1'bz;  // Controlled_Buffer controlled_buffer_7
  assign in_3 = and_11_out ? in_12 : 1'bz;  // Controlled_Buffer controlled_buffer_8
  assign in_4 = and_11_out ? in_13 : 1'bz;  // Controlled_Buffer controlled_buffer_9
  assign in_25 = and_12_out ? in_14 : 1'bz;  // Controlled_Buffer controlled_buffer_10
  assign in_27 = and_12_out ? in_16 : 1'bz;  // Controlled_Buffer controlled_buffer_11
  assign in_28 = and_12_out ? in_18 : 1'bz;  // Controlled_Buffer controlled_buffer_12
  assign in_29 = and_12_out ? in_20 : 1'bz;  // Controlled_Buffer controlled_buffer_13
  assign in_1 = and_12_out ? in_22 : 1'bz;  // Controlled_Buffer controlled_buffer_14
  assign in_2 = and_12_out ? in_23 : 1'bz;  // Controlled_Buffer controlled_buffer_15
  assign in_3 = and_12_out ? in_24 : 1'bz;  // Controlled_Buffer controlled_buffer_16
  assign in_4 = and_12_out ? in_26 : 1'bz;  // Controlled_Buffer controlled_buffer_17
  assign in_25 = and_13_out ? in_30 : 1'bz;  // Controlled_Buffer controlled_buffer_18
  assign in_27 = and_13_out ? in_31 : 1'bz;  // Controlled_Buffer controlled_buffer_19
  assign in_28 = and_13_out ? in_32 : 1'bz;  // Controlled_Buffer controlled_buffer_20
  assign in_29 = and_13_out ? in_33 : 1'bz;  // Controlled_Buffer controlled_buffer_21
  assign in_1 = and_13_out ? in_34 : 1'bz;  // Controlled_Buffer controlled_buffer_22
  assign in_2 = and_13_out ? in_35 : 1'bz;  // Controlled_Buffer controlled_buffer_23
  assign in_3 = and_13_out ? in_36 : 1'bz;  // Controlled_Buffer controlled_buffer_24
  assign in_4 = and_13_out ? in_37 : 1'bz;  // Controlled_Buffer controlled_buffer_25
  assign in_25 = and_14_out ? in_38 : 1'bz;  // Controlled_Buffer controlled_buffer_26
  assign in_27 = and_14_out ? in_39 : 1'bz;  // Controlled_Buffer controlled_buffer_27
  assign in_28 = and_14_out ? in_40 : 1'bz;  // Controlled_Buffer controlled_buffer_28
  assign in_29 = and_14_out ? in_41 : 1'bz;  // Controlled_Buffer controlled_buffer_29
  assign in_1 = and_14_out ? in_42 : 1'bz;  // Controlled_Buffer controlled_buffer_30
  assign in_2 = and_14_out ? in_43 : 1'bz;  // Controlled_Buffer controlled_buffer_31
  assign in_3 = and_14_out ? in_44 : 1'bz;  // Controlled_Buffer controlled_buffer_32
  assign in_4 = and_14_out ? in_45 : 1'bz;  // Controlled_Buffer controlled_buffer_33
  assign in_25 = and_15_out ? in_46 : 1'bz;  // Controlled_Buffer controlled_buffer_34
  assign in_27 = and_15_out ? in_47 : 1'bz;  // Controlled_Buffer controlled_buffer_35
  assign in_28 = and_15_out ? in_48 : 1'bz;  // Controlled_Buffer controlled_buffer_36
  assign in_29 = and_15_out ? in_49 : 1'bz;  // Controlled_Buffer controlled_buffer_37
  assign in_1 = and_15_out ? in_50 : 1'bz;  // Controlled_Buffer controlled_buffer_38
  assign in_2 = and_15_out ? in_51 : 1'bz;  // Controlled_Buffer controlled_buffer_39
  assign in_3 = and_15_out ? in_52 : 1'bz;  // Controlled_Buffer controlled_buffer_40
  assign in_4 = and_15_out ? in_53 : 1'bz;  // Controlled_Buffer controlled_buffer_41
  and and_1 (and_1_out, not_5_out, out_58);
  and and_2 (and_2_out, not_7_out, out_66);
  and and_3 (and_3_out, not_8_out, not_7_out);
  and and_4 (and_4_out, not_5_out, out_58);
  and and_5 (and_5_out, not_6_out, not_5_out);
  and and_6 (and_6_out, out_62, out_66);
  and and_7 (and_7_out, not_6_out, not_5_out);
  and and_8 (and_8_out, out_62, not_8_out);
  and and_9 (and_9_out, not_5_out, not_6_out);
  and and_10 (and_10_out, not_7_out, out_66);
  and and_11 (and_11_out, and_1_out, and_2_out);
  and and_12 (and_12_out, and_3_out, and_4_out);
  and and_13 (and_13_out, and_5_out, and_6_out);
  and and_14 (and_14_out, and_7_out, and_8_out);
  and and_15 (and_15_out, and_9_out, and_10_out);
  not not_9 (not_9_out, in_1);
  not not_10 (not_10_out, in_2);
  not not_11 (not_11_out, in_3);
  not not_12 (not_12_out, in_4);
  and and_16 (and_16_out, not_9_out, in_2);
  and and_17 (and_17_out, not_11_out, in_4);
  and and_18 (and_18_out, not_12_out, not_11_out);
  and and_19 (and_19_out, not_9_out, in_2);
  and and_20 (and_20_out, not_10_out, not_9_out);
  and and_21 (and_21_out, in_3, in_4);
  and and_22 (and_22_out, not_10_out, not_9_out);
  and and_23 (and_23_out, in_3, not_12_out);
  and and_24 (and_24_out, not_9_out, not_10_out);
  and and_25 (and_25_out, not_11_out, in_4);
  not not_13 (not_13_out, in_25);
  not not_14 (not_14_out, in_27);
  not not_15 (not_15_out, in_28);
  not not_16 (not_16_out, in_29);
  and and_26 (and_26_out, and_16_out, and_17_out);
  and and_27 (and_27_out, and_18_out, and_19_out);
  and and_28 (and_28_out, and_20_out, and_21_out);
  and and_29 (and_29_out, and_22_out, and_23_out);
  and and_30 (and_30_out, and_24_out, and_25_out);
  and and_31 (and_31_out, and_29_out, not_13_out);
  and and_32 (and_32_out, in_25, and_29_out);
  and and_33 (and_33_out, and_29_out, not_14_out);
  and and_34 (and_34_out, in_27, and_29_out);
  and and_35 (and_35_out, and_29_out, not_15_out);
  and and_36 (and_36_out, in_28, and_29_out);
  and and_37 (and_37_out, and_29_out, not_16_out);
  and and_38 (and_38_out, in_29, and_29_out);
  nor nor_1 (out_75, and_31_out, nor_2_out);
  nor nor_2 (nor_2_out, out_75, and_32_out);
  nor nor_3 (out_76, and_33_out, nor_4_out);
  nor nor_4 (nor_4_out, out_76, and_34_out);
  nor nor_5 (out_77, and_35_out, nor_6_out);
  nor nor_6 (nor_6_out, out_77, and_36_out);
  nor nor_7 (out_78, and_37_out, nor_8_out);
  nor nor_8 (nor_8_out, out_78, and_38_out);
  nor nor_9 (nor_9_out, nor_10_out, and_27_out);
  nor nor_10 (nor_10_out, and_28_out, nor_9_out);
  xor xor_1 (xor_1_out, nor_10_out, out_75);
  xor xor_2 (xor_2_out, out_76, nor_10_out);
  xor xor_3 (xor_3_out, nor_10_out, out_77);
  xor xor_4 (xor_4_out, out_78, nor_10_out);
  and and_39 (and_39_out, in_21, xor_4_out);
  xor xor_5 (xor_5_out, in_21, xor_4_out);
  and and_40 (and_40_out, xor_5_out, nor_10_out);
  xor xor_6 (out_69, xor_5_out, nor_10_out);
  or or_1 (CAR_4, and_39_out, and_40_out);
  not not_17 (not_17_out, and_30_out);
  not not_18 (not_18_out, and_30_out);
  not not_19 (not_19_out, and_30_out);
  not not_20 (not_20_out, and_30_out);
  not not_21 (not_21_out, out_73);
  not not_22 (not_22_out, out_69);
  not not_23 (not_23_out, out_71);
  not not_24 (not_24_out, out_72);
  and and_41 (and_41_out, in_19, xor_3_out);
  xor xor_7 (xor_7_out, in_19, xor_3_out);
  and and_42 (and_42_out, not_19_out, not_21_out);
  and and_43 (and_43_out, out_73, not_19_out);
  and and_44 (and_44_out, not_20_out, not_22_out);
  and and_45 (and_45_out, out_69, not_20_out);
  and and_46 (and_46_out, not_17_out, not_23_out);
  and and_47 (and_47_out, out_71, not_17_out);
  and and_48 (and_48_out, not_18_out, not_24_out);
  and and_49 (and_49_out, out_72, not_18_out);
  and and_50 (and_50_out, xor_7_out, CAR_4);
  xor xor_8 (out_73, xor_7_out, CAR_4);
  nor nor_11 (nor_11_out, and_42_out, nor_12_out);
  nor nor_12 (nor_12_out, nor_11_out, and_43_out);
  nor nor_13 (nor_13_out, and_44_out, nor_14_out);
  nor nor_14 (nor_14_out, nor_13_out, and_45_out);
  or or_2 (CAR_3, and_41_out, and_50_out);
  nor nor_15 (nor_15_out, and_46_out, nor_16_out);
  nor nor_16 (nor_16_out, nor_15_out, and_47_out);
  nor nor_17 (nor_17_out, and_48_out, nor_18_out);
  nor nor_18 (nor_18_out, nor_17_out, and_49_out);
  not not_25 (not_25_out, nor_11_out);
  not not_26 (not_26_out, nor_13_out);
  and and_51 (and_51_out, in_17, xor_2_out);
  xor xor_9 (xor_9_out, in_17, xor_2_out);
  not not_27 (not_27_out, nor_15_out);
  not not_28 (not_28_out, nor_17_out);
  and and_52 (and_52_out, and_30_out, not_25_out);
  and and_53 (and_53_out, nor_11_out, and_30_out);
  and and_54 (and_54_out, and_30_out, not_26_out);
  and and_55 (and_55_out, nor_13_out, and_30_out);
  and and_56 (and_56_out, and_30_out, not_27_out);
  and and_57 (and_57_out, nor_15_out, and_30_out);
  and and_58 (and_58_out, and_30_out, not_28_out);
  and and_59 (and_59_out, nor_17_out, and_30_out);
  and and_60 (and_60_out, xor_9_out, CAR_3);
  xor xor_10 (out_72, xor_9_out, CAR_3);
  or or_3 (CAR_2, and_51_out, and_60_out);
  nor nor_19 (out_79, and_56_out, nor_25_out);
  nor nor_20 (out_81, and_58_out, nor_26_out);
  nor nor_21 (out_83, and_52_out, nor_22_out);
  nor nor_22 (nor_22_out, out_83, and_53_out);
  nor nor_23 (out_85, and_54_out, nor_24_out);
  nor nor_24 (nor_24_out, out_85, and_55_out);
  nor nor_25 (nor_25_out, out_79, and_57_out);
  nor nor_26 (nor_26_out, out_81, and_59_out);
  and and_61 (and_61_out, in_15, xor_1_out);
  xor xor_11 (xor_11_out, in_15, xor_1_out);
  and and_62 (and_62_out, xor_11_out, CAR_2);
  xor xor_12 (out_71, xor_11_out, CAR_2);
  or or_4 (CAR, and_61_out, and_62_out);
  not not_29 (not_29_out, out_79);
  not not_30 (not_30_out, out_81);
  not not_31 (not_31_out, out_83);
  not not_32 (not_32_out, out_85);
  and and_63 (and_63_out, and_26_out, not_29_out);
  and and_64 (and_64_out, out_79, and_26_out);
  and and_65 (and_65_out, and_26_out, not_30_out);
  and and_66 (and_66_out, out_81, and_26_out);
  and and_67 (and_67_out, and_26_out, not_31_out);
  and and_68 (and_68_out, out_83, and_26_out);
  and and_69 (and_69_out, and_26_out, not_32_out);
  and and_70 (and_70_out, out_85, and_26_out);
  nor nor_27 (out_80, and_63_out, nor_28_out);
  nor nor_28 (nor_28_out, out_80, and_64_out);
  nor nor_29 (out_82, and_65_out, nor_30_out);
  nor nor_30 (nor_30_out, out_82, and_66_out);
  nor nor_31 (out_84, and_67_out, nor_32_out);
  nor nor_32 (nor_32_out, out_84, and_68_out);
  nor nor_33 (out_86, and_69_out, nor_34_out);
  nor nor_34 (nor_34_out, out_86, and_70_out);

  assign out_70 = CAR;
  assign SUM = out_71;
  assign SUM_2 = out_72;
  assign SUM_3 = out_73;
  assign SUM_4 = out_69;

  // Notes on the sheet:
  //   OPCODE REG
  //   DATA BUS
  //   DISPLAY
  //   SUBTRACT
  //   ADD
  //   INSCRUCT STORE
  //   ACCU STORE
  //   CNTRL UNIT
  //   DISPLAY
  //   SUBTRACT
  //   ADD
  //   INSCRUCT STORE
  //   ACCU STORE
  //   iNSTRUCTION REG
  //   SUB VS ADD
  //   A
  //   B
  //   CAR
  //   A
  //   B
  //   CAR
  //   ALU
  //   ACC
  //   A
  //   B
  //   CAR
  //   A
  //   B
  //   CAR
  //   DLATCH REG
endmodule
